# Fritzing sketch spark_button_led (saved by Fritzing 0.8.7b)
breadboards: 1

parts:
  U1 = Spark Core (v1.0)
  S1 = Pushbutton [package="[THT]"]
  R1 = Resistor [package="2512 [SMD]"]

nets:
  N1: U1.A2, U1.3V3
  N2: U1.A3, U1.A6
  N3: U1.A5, U1.VIN
  N4: U1.GND, R1.Pin_1
  N5: U1.D7, S1.Pin_1, S1.Pin_2, R1.Pin_0
  N6: U1.3V3*, S1.Pin_3, S1.Pin_4

custom parts:
  Spark Core (v1.0): The Spark Core is a tiny Wi-Fi development board that makes it easy to create internet-connected hardware. The Core is all you need to get started; power it over USB and in minutes you'll be controlling LEDs, switches and motors and collecting data from sensors over the internet! It has 8 digital I/O pins, 8 analog I/O pins, 8 PWM pins; UART (Serial), SPI, I2C, and JTAG peripherals available.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
